// Logisim project 06532025_Lab5.circ as structural Verilog
module project_ro (
  input  [15:0] A,
  input  [15:0] B,
  input  [2:0] selectors,
  output result
);

  wire comparator_1_eq, comparator_1_gt, comparator_1_lt, not_1_out, or_1_out, or_2_out;

  Comparator #(.mode("unsigned"), .width(16)) comparator_1 (
    .a(A), .b(B), .gt(comparator_1_gt), .eq(comparator_1_eq), .lt(comparator_1_lt));
  or or_1 (or_1_out, comparator_1_gt, comparator_1_eq);
  or or_2 (or_2_out, comparator_1_eq, comparator_1_lt);
  not not_1 (not_1_out, comparator_1_eq);
  Multiplexer #(.select(3)) multiplexer_1 (
    .in0(or_1_out), .in1(comparator_1_gt), .in2(comparator_1_eq), .in3(comparator_1_lt), .in4(or_2_out),
    .in5(not_1_out), .out(result), .sel(selectors));  // open: in6, in7

  // Notes on the sheet:
  //   Logic Unit (LU)
  //   >=
  //   >
  //   =
  //   <
  //   <=
  //   !=
endmodule
