// Logisim project COA_FINAL_LOGISIM.circ as structural Verilog
module project_ao (
  input  [15:0] A,
  input  [3:0] AUSel,
  input  [15:0] B,
  output [15:0] AUResult
);

  wire [15:0] adder_1_out, and_1_out, divider_1_out, divider_2_rem, multiplier_1_out, negator_1_out,
       negator_2_out, or_1_out, shifter_1_out, shifter_2_out, shifter_3_out, shifter_4_out, subtractor_1_out,
       xor_1_out;

  Adder #(.width(16)) adder_1 (.a(A), .b(B), .out(adder_1_out));  // open: cin, cout
  assign and_1_out = A & B;  // AND_Gate and_1, 16 bits wide
  assign or_1_out = A | B;  // OR_Gate or_1, 16 bits wide
  assign xor_1_out = A ^ B;  // XOR_Gate xor_1, 16 bits wide
  Divider #(.width(16)) divider_1 (.a(A), .b(B), .out(divider_1_out));  // open: upper, rem
  Divider #(.width(16)) divider_2 (.a(A), .b(B), .rem(divider_2_rem));  // open: out, upper
  Multiplier #(.width(16)) multiplier_1 (.a(A), .b(B), .out(multiplier_1_out));  // open: cin, cout
  Subtractor #(.width(16)) subtractor_1 (.a(A), .b(B), .out(subtractor_1_out));  // open: bin, bout
  Shifter #(.width(16)) shifter_1 (.in(A), .\dist (4'b0010), .out(shifter_1_out));
  Shifter #(.width(16)) shifter_2 (.in(B), .\dist (4'b0010), .out(shifter_2_out));
  Shifter #(.shift("lr"), .width(16)) shifter_3 (.in(A), .\dist (4'b0010), .out(shifter_3_out));
  Shifter #(.shift("lr"), .width(16)) shifter_4 (.in(B), .\dist (4'b0010), .out(shifter_4_out));
  Negator #(.width(16)) negator_1 (.in(A), .out(negator_1_out));
  Negator #(.width(16)) negator_2 (.in(B), .out(negator_2_out));
  Multiplexer #(.select(4), .width(16)) multiplexer_1 (
    .in0(adder_1_out), .in1(and_1_out), .in2(or_1_out), .in3(xor_1_out), .in4(divider_1_out),
    .in5(divider_2_rem), .in6(multiplier_1_out), .in7(subtractor_1_out), .in8(shifter_1_out),
    .in9(shifter_2_out), .in10(shifter_3_out), .in11(shifter_4_out), .in12(negator_1_out),
    .in13(negator_2_out), .out(AUResult), .sel(AUSel));  // open: in14, in15
endmodule

module project_ro (
  input  [15:0] A,
  input  [15:0] B,
  input  [2:0] RUSel,
  output result
);

  wire comparator_1_eq, comparator_1_gt, comparator_1_lt, not_1_out, or_1_out, or_2_out;

  Comparator #(.mode("unsigned"), .width(16)) comparator_1 (
    .a(A), .b(B), .gt(comparator_1_gt), .eq(comparator_1_eq), .lt(comparator_1_lt));
  or or_1 (or_1_out, comparator_1_gt, comparator_1_eq);
  or or_2 (or_2_out, comparator_1_eq, comparator_1_lt);
  not not_1 (not_1_out, comparator_1_eq);
  Multiplexer #(.select(3)) multiplexer_1 (
    .in0(or_1_out), .in1(comparator_1_gt), .in2(comparator_1_eq), .in3(comparator_1_lt), .in4(or_2_out),
    .in5(not_1_out), .out(result), .sel(RUSel));  // open: in6, in7

  // Notes on the sheet:
  //   Logic Unit (LU)
  //   >=
  //   >
  //   =
  //   <
  //   <=
  //   !=
endmodule

module project_alu (
  input  [15:0] A,
  input  [15:0] B,
  input  [3:0] au_sel,
  input  [2:0] ru_sel,
  input  OE,
  output [15:0] AUDout,
  output [15:0] AUResult,
  output RUResult
);

  project_ao project_ao_1 (.A(A), .AUSel(au_sel), .B(B), .AUResult(AUResult));
  project_ro project_ro_1 (.A(A), .B(B), .RUSel(ru_sel), .result(RUResult));
  assign AUDout = OE ? AUResult : 16'bz;  // Controlled_Buffer controlled_buffer_1
endmodule

module reg16bit (
  input  [15:0] Din,
  input  we,
  input  clk,
  input  reset,
  input  oe,
  output [15:0] SD,
  output [15:0] Dout,
  output [7:0] out_8,
  output [7:0] out_9
);

  Register #(.width(16)) register_1 (.D(Din), .en(we), .clk(clk), .Q(SD), .clr(reset));
  assign Dout = oe ? SD : 16'bz;  // Controlled_Buffer controlled_buffer_1
  BitSelector #(.group(8), .width(16)) bitselector_1 (.in(Dout), .out(out_8), .sel(1'b0));
  BitSelector #(.group(8), .width(16)) bitselector_2 (.in(Dout), .out(out_9), .sel(1'b1));
endmodule

module datapath (
  input  [15:0] test_data,
  input  we_mar,
  input  oe_test,
  input  oe_mar,
  input  intrnl_oe_mar,
  input  we_mbr,
  input  oe_mbr,
  input  we_ir,
  input  reset_ir,
  input  oe_ir,
  input  we_rega,
  input  reset_rega,
  input  [3:0] au_sel,
  input  we_or,
  input  [2:0] ru_sel,
  input  oe_alu,
  input  oe_or,
  input  we_regb,
  input  reset_regb,
  output [7:0] content_mar,
  output [15:0] content_ir,
  output [15:0] out_22,
  output [15:0] sd_rega,
  output [15:0] out_24,
  output [15:0] sd_or,
  output out_26,
  output [15:0] sd_regb
);

  wire clock_1_out;
  wire [7:0] bitselector_1_out, reg8bit_1_dout;
  wire [15:0] project_alu_1_audout, reg16bit_1_dout, reg16bit_2_dout;

  Clock clock_1 (.out(clock_1_out));
  LED D15 (.in(project_alu_1_audout[15]));
  BitSelector #(.group(8), .width(16)) bitselector_1 (.in(reg16bit_1_dout), .out(bitselector_1_out), .sel(1'b0));
  reg16bit reg16bit_1 (
    .Din(project_alu_1_audout), .we(we_ir), .clk(clock_1_out), .reset(reset_ir), .oe(oe_ir), .SD(content_ir),
    .Dout(reg16bit_1_dout));  // open: out_8, out_9
  reg16bit reg16bit_2 (
    .Din(project_alu_1_audout), .we(we_rega), .clk(clock_1_out), .reset(reset_rega), .SD(sd_rega),
    .Dout(reg16bit_2_dout));  // open: oe, out_8, out_9
  project_alu project_alu_1 (
    .A(sd_rega), .B(sd_regb), .au_sel(au_sel), .ru_sel(ru_sel), .OE(oe_alu), .AUDout(project_alu_1_audout),
    .AUResult(out_24), .RUResult(out_26));
  reg16bit reg16bit_3 (
    .Din(project_alu_1_audout), .we(we_regb), .clk(clock_1_out), .reset(reset_regb), .SD(sd_regb));  // open: oe, Dout, out_8, out_9
  LED D14 (.in(project_alu_1_audout[14]));
  LED D13 (.in(project_alu_1_audout[13]));
  LED D12 (.in(project_alu_1_audout[12]));
  LED D11 (.in(project_alu_1_audout[11]));
  LED D10 (.in(project_alu_1_audout[10]));
  assign project_alu_1_audout = oe_test ? test_data : 16'bz;  // Controlled_Buffer controlled_buffer_1
  LED D9 (.in(project_alu_1_audout[9]));
  LED D8 (.in(project_alu_1_audout[8]));
  LED D7 (.in(project_alu_1_audout[7]));
  LED D6 (.in(project_alu_1_audout[6]));
  LED D5 (.in(project_alu_1_audout[5]));
  LED D4 (.in(project_alu_1_audout[4]));
  LED D3 (.in(project_alu_1_audout[3]));
  assign project_alu_1_audout = intrnl_oe_mar ? out_22 : 16'bz;  // Controlled_Buffer controlled_buffer_2
  LED D2 (.in(project_alu_1_audout[2]));
  LED D1 (.in(project_alu_1_audout[1]));
  LED D0 (.in(project_alu_1_audout[0]));
  reg8bit reg8bit_1 (
    .Din(bitselector_1_out), .we(we_mar), .clk(clock_1_out), .oe(oe_mar), .SD(content_mar),
    .Dout(reg8bit_1_dout));  // open: reset
  reg16bit reg16bit_4 (
    .Din(project_alu_1_audout), .we(we_mbr), .clk(clock_1_out), .oe(oe_mbr), .SD(out_22),
    .Dout(project_alu_1_audout));  // open: reset, out_8, out_9
  reg16bit reg16bit_5 (
    .Din(project_alu_1_audout), .we(we_or), .clk(clock_1_out), .oe(oe_or), .SD(sd_or),
    .Dout(project_alu_1_audout));  // open: reset, out_8, out_9
  LED led_1 (.in(project_alu_1_audout[15]));
  LED led_2 (.in(project_alu_1_audout[14]));
  LED led_3 (.in(project_alu_1_audout[13]));
  LED led_4 (.in(project_alu_1_audout[12]));
  LED led_5 (.in(project_alu_1_audout[11]));
  LED led_6 (.in(project_alu_1_audout[10]));
  LED led_7 (.in(project_alu_1_audout[9]));
  LED led_8 (.in(project_alu_1_audout[8]));
  LED led_9 (.in(project_alu_1_audout[7]));
  LED led_10 (.in(project_alu_1_audout[6]));
  LED led_11 (.in(project_alu_1_audout[5]));
  LED led_12 (.in(project_alu_1_audout[4]));
  LED led_13 (.in(project_alu_1_audout[3]));
  LED led_14 (.in(project_alu_1_audout[2]));
  LED led_15 (.in(project_alu_1_audout[1]));
  LED led_16 (.in(project_alu_1_audout[0]));

  // Notes on the sheet:
  //   Instruction Register
  //   registerA
  //   ALU
  //   registerB
  //   Internal Address Bus (8-bits)
  //   MAR
  //   MBR
  //   Output Register
endmodule

module reg8bit (
  input  [7:0] Din,
  input  we,
  input  clk,
  input  reset,
  input  oe,
  output [7:0] SD,
  output [7:0] Dout
);

  Register register_1 (.D(Din), .en(we), .clk(clk), .Q(SD), .clr(reset));
  assign Dout = oe ? SD : 8'bz;  // Controlled_Buffer controlled_buffer_1
endmodule

module CPU (
  input  oe_counter,
  input  test_oe,
  input  we_ram,
  input  [7:0] in_4,
  input  ce_counter,
  input  [15:0] test_data,
  input  we_mar,
  input  oe_test,
  input  oe_mar,
  input  intrnl_oe_mar,
  input  we_mbr,
  input  oe_ram,
  input  oe_mbr,
  input  we_ir,
  input  reset_ir,
  input  oe_ir,
  input  we_rega,
  input  reset_rega,
  input  we_or,
  input  [3:0] au_sel,
  input  [2:0] ru_sel,
  input  oe_or,
  input  oe_alu,
  input  we_regb,
  input  reset_regb,
  output [7:0] out_26,
  output [7:0] content_mar,
  output [15:0] content_ir,
  output [15:0] out_29,
  output [15:0] sd_rega,
  output [15:0] sd_or,
  output [15:0] out_32,
  output out_33,
  output [15:0] sd_regb
);

  wire clock_1_out;
  wire [7:0] controlled_buffer_1_out, reg8bit_1_dout;
  wire [15:0] bit_extender_1_out, decimal_encoder_2_dout, project_alu_1_audout, ram_1_dout, reg16bit_1_dout,
       reg16bit_2_dout;
  wire [31:0] decimal_encoder_1_dout, decimal_encoder_3_dout, decimal_encoder_4_dout;
  wire [31:16] decimal_encoder_2_dout_2;

  decimal_encoder decimal_encoder_1 (.Din(sd_rega), .Dout(decimal_encoder_1_dout));
  _7_Segment_Display u_7_segment_display_1 (
    .g(decimal_encoder_2_dout[3]), .f(decimal_encoder_2_dout[2]), .a(decimal_encoder_2_dout[1]),
    .b(decimal_encoder_2_dout[0]), .e(decimal_encoder_2_dout_2[19]), .d(decimal_encoder_2_dout_2[18]),
    .c(decimal_encoder_2_dout_2[17]), .dp(decimal_encoder_2_dout_2[16]));
  decimal_encoder decimal_encoder_2 (
    .Din(bit_extender_1_out), .Dout({decimal_encoder_2_dout_2, decimal_encoder_2_dout}));
  _7_Segment_Display u_7_segment_display_2 (
    .g(decimal_encoder_1_dout[15]), .f(decimal_encoder_1_dout[14]), .a(decimal_encoder_1_dout[13]),
    .b(decimal_encoder_1_dout[12]), .e(decimal_encoder_1_dout[31]), .d(decimal_encoder_1_dout[30]),
    .c(decimal_encoder_1_dout[29]), .dp(decimal_encoder_1_dout[28]));
  _7_Segment_Display u_7_segment_display_3 (
    .g(decimal_encoder_1_dout[11]), .f(decimal_encoder_1_dout[10]), .a(decimal_encoder_1_dout[9]),
    .b(decimal_encoder_1_dout[8]), .e(decimal_encoder_1_dout[27]), .d(decimal_encoder_1_dout[26]),
    .c(decimal_encoder_1_dout[25]), .dp(decimal_encoder_1_dout[24]));
  decimal_encoder decimal_encoder_3 (.Din(sd_regb), .Dout(decimal_encoder_3_dout));
  _7_Segment_Display u_7_segment_display_4 (
    .g(decimal_encoder_1_dout[7]), .f(decimal_encoder_1_dout[6]), .a(decimal_encoder_1_dout[5]),
    .b(decimal_encoder_1_dout[4]), .e(decimal_encoder_1_dout[23]), .d(decimal_encoder_1_dout[22]),
    .c(decimal_encoder_1_dout[21]), .dp(decimal_encoder_1_dout[20]));
  _7_Segment_Display u_7_segment_display_5 (
    .g(decimal_encoder_1_dout[3]), .f(decimal_encoder_1_dout[2]), .a(decimal_encoder_1_dout[1]),
    .b(decimal_encoder_1_dout[0]), .e(decimal_encoder_1_dout[19]), .d(decimal_encoder_1_dout[18]),
    .c(decimal_encoder_1_dout[17]), .dp(decimal_encoder_1_dout[16]));
  _7_Segment_Display u_7_segment_display_6 (
    .g(decimal_encoder_3_dout[15]), .f(decimal_encoder_3_dout[14]), .a(decimal_encoder_3_dout[13]),
    .b(decimal_encoder_3_dout[12]), .e(decimal_encoder_3_dout[31]), .d(decimal_encoder_3_dout[30]),
    .c(decimal_encoder_3_dout[29]), .dp(decimal_encoder_3_dout[28]));
  _7_Segment_Display u_7_segment_display_7 (
    .g(decimal_encoder_3_dout[11]), .f(decimal_encoder_3_dout[10]), .a(decimal_encoder_3_dout[9]),
    .b(decimal_encoder_3_dout[8]), .e(decimal_encoder_3_dout[27]), .d(decimal_encoder_3_dout[26]),
    .c(decimal_encoder_3_dout[25]), .dp(decimal_encoder_3_dout[24]));
  _7_Segment_Display u_7_segment_display_8 (
    .g(decimal_encoder_3_dout[7]), .f(decimal_encoder_3_dout[6]), .a(decimal_encoder_3_dout[5]),
    .b(decimal_encoder_3_dout[4]), .e(decimal_encoder_3_dout[23]), .d(decimal_encoder_3_dout[22]),
    .c(decimal_encoder_3_dout[21]), .dp(decimal_encoder_3_dout[20]));
  _7_Segment_Display u_7_segment_display_9 (
    .g(decimal_encoder_3_dout[3]), .f(decimal_encoder_3_dout[2]), .a(decimal_encoder_3_dout[1]),
    .b(decimal_encoder_3_dout[0]), .e(decimal_encoder_3_dout[19]), .d(decimal_encoder_3_dout[18]),
    .c(decimal_encoder_3_dout[17]), .dp(decimal_encoder_3_dout[16]));
  Counter Program_Counter (
    .count(ce_counter), .clk(clock_1_out), .D(controlled_buffer_1_out), .Q(out_26));  // open: clr, load, up, carry
  Clock clock_1 (.out(clock_1_out));
  assign controlled_buffer_1_out = oe_counter ? out_26 : 8'bz;  // Controlled_Buffer controlled_buffer_1
  assign bit_extender_1_out = {{8{out_26[7]}}, out_26};  // Bit_Extender bit_extender_1
  BitSelector #(.group(8), .width(16)) bitselector_1 (.in(reg16bit_1_dout), .out(controlled_buffer_1_out), .sel(1'b0));
  reg16bit reg16bit_1 (
    .Din(project_alu_1_audout), .we(we_ir), .clk(clock_1_out), .reset(reset_ir), .oe(oe_ir), .SD(content_ir),
    .Dout(reg16bit_1_dout));  // open: out_8, out_9
  reg16bit reg16bit_2 (
    .Din(project_alu_1_audout), .we(we_rega), .clk(clock_1_out), .reset(reset_rega), .SD(sd_rega),
    .Dout(reg16bit_2_dout));  // open: oe, out_8, out_9
  project_alu project_alu_1 (
    .A(sd_rega), .B(sd_regb), .au_sel(au_sel), .ru_sel(ru_sel), .OE(oe_alu), .AUDout(project_alu_1_audout),
    .AUResult(out_32), .RUResult(out_33));
  reg16bit reg16bit_3 (
    .Din(project_alu_1_audout), .we(we_regb), .clk(clock_1_out), .reset(reset_regb), .SD(sd_regb));  // open: oe, Dout, out_8, out_9
  LED D15 (.in(project_alu_1_audout[15]));
  LED D14 (.in(project_alu_1_audout[14]));
  LED D13 (.in(project_alu_1_audout[13]));
  LED D12 (.in(project_alu_1_audout[12]));
  LED D11 (.in(project_alu_1_audout[11]));
  LED D10 (.in(project_alu_1_audout[10]));
  LED D9 (.in(project_alu_1_audout[9]));
  LED D8 (.in(project_alu_1_audout[8]));
  assign project_alu_1_audout = oe_test ? test_data : 16'bz;  // Controlled_Buffer controlled_buffer_2
  LED D7 (.in(project_alu_1_audout[7]));
  LED D6 (.in(project_alu_1_audout[6]));
  LED D5 (.in(project_alu_1_audout[5]));
  LED D4 (.in(project_alu_1_audout[4]));
  assign project_alu_1_audout = intrnl_oe_mar ? out_29 : 16'bz;  // Controlled_Buffer controlled_buffer_3
  LED D3 (.in(project_alu_1_audout[3]));
  LED D2 (.in(project_alu_1_audout[2]));
  LED D1 (.in(project_alu_1_audout[1]));
  LED D0 (.in(project_alu_1_audout[0]));
  reg8bit reg8bit_1 (
    .Din(controlled_buffer_1_out), .we(we_mar), .clk(clock_1_out), .oe(oe_mar), .SD(content_mar),
    .Dout(reg8bit_1_dout));  // open: reset
  reg16bit reg16bit_4 (
    .Din(project_alu_1_audout), .we(we_mbr), .clk(clock_1_out), .oe(oe_mbr), .SD(out_29),
    .Dout(project_alu_1_audout));  // open: reset, out_8, out_9
  reg16bit reg16bit_5 (
    .Din(project_alu_1_audout), .we(we_or), .clk(clock_1_out), .oe(oe_or), .SD(sd_or),
    .Dout(project_alu_1_audout));  // open: reset, out_8, out_9
  assign reg8bit_1_dout = test_oe ? in_4 : 8'bz;  // Controlled_Buffer controlled_buffer_4
  LED led_1 (.in(project_alu_1_audout[15]));
  LED led_2 (.in(project_alu_1_audout[14]));
  LED led_3 (.in(project_alu_1_audout[13]));
  LED led_4 (.in(project_alu_1_audout[12]));
  LED led_5 (.in(project_alu_1_audout[11]));
  LED led_6 (.in(project_alu_1_audout[10]));
  LED led_7 (.in(project_alu_1_audout[9]));
  LED led_8 (.in(project_alu_1_audout[8]));
  LED led_9 (.in(project_alu_1_audout[7]));
  LED led_10 (.in(project_alu_1_audout[6]));
  LED led_11 (.in(project_alu_1_audout[5]));
  decimal_encoder decimal_encoder_4 (.Din(sd_or), .Dout(decimal_encoder_4_dout));
  LED led_12 (.in(project_alu_1_audout[4]));
  LED led_13 (.in(project_alu_1_audout[3]));
  LED led_14 (.in(project_alu_1_audout[2]));
  LED led_15 (.in(project_alu_1_audout[1]));
  _7_Segment_Display u_7_segment_display_10 (
    .g(decimal_encoder_4_dout[15]), .f(decimal_encoder_4_dout[14]), .a(decimal_encoder_4_dout[13]),
    .b(decimal_encoder_4_dout[12]), .e(decimal_encoder_4_dout[31]), .d(decimal_encoder_4_dout[30]),
    .c(decimal_encoder_4_dout[29]), .dp(decimal_encoder_4_dout[28]));
  LED led_16 (.in(project_alu_1_audout[0]));
  _7_Segment_Display u_7_segment_display_11 (
    .g(decimal_encoder_4_dout[11]), .f(decimal_encoder_4_dout[10]), .a(decimal_encoder_4_dout[9]),
    .b(decimal_encoder_4_dout[8]), .e(decimal_encoder_4_dout[27]), .d(decimal_encoder_4_dout[26]),
    .c(decimal_encoder_4_dout[25]), .dp(decimal_encoder_4_dout[24]));
  _7_Segment_Display u_7_segment_display_12 (
    .g(decimal_encoder_4_dout[7]), .f(decimal_encoder_4_dout[6]), .a(decimal_encoder_4_dout[5]),
    .b(decimal_encoder_4_dout[4]), .e(decimal_encoder_4_dout[23]), .d(decimal_encoder_4_dout[22]),
    .c(decimal_encoder_4_dout[21]), .dp(decimal_encoder_4_dout[20]));
  _7_Segment_Display u_7_segment_display_13 (
    .g(decimal_encoder_4_dout[3]), .f(decimal_encoder_4_dout[2]), .a(decimal_encoder_4_dout[1]),
    .b(decimal_encoder_4_dout[0]), .e(decimal_encoder_4_dout[19]), .d(decimal_encoder_4_dout[18]),
    .c(decimal_encoder_4_dout[17]), .dp(decimal_encoder_4_dout[16]));
  RAM #(.dataWidth(16), .enables("line")) ram_1 (
    .addr(reg8bit_1_dout), .we(we_ram), .clk(clock_1_out), .din(project_alu_1_audout), .dout(ram_1_dout));
  assign project_alu_1_audout = oe_ram ? ram_1_dout : 16'bz;  // Controlled_Buffer controlled_buffer_5

  // Notes on the sheet:
  //   Instruction Register
  //   registerA
  //   ALU
  //   registerB
  //   Internal Address Bus (8-bits)
  //   Internal Address Bus 
  //   MAR
  //   MBR
  //   Output Register
  //   External Address Bus (8-bits)
endmodule

module decimal_encoder (
  input  [15:0] Din,
  output [31:0] Dout
);

  ROM #(.addrWidth(16), .dataWidth(32)) rom_1 (
    .addr(Din),
    .data({Dout[31:28], Dout[15:12], Dout[27:24], Dout[11:8], Dout[23:20], Dout[7:4], Dout[19:16], Dout[3:0]}));

  // Notes on the sheet:
  //   contents of rom_1 (hex, n*v repeats v):
  //   e7 21 cb 6b 2d 6e ee 23 ef 2f 21e7 2121 21cb 216b 212d 216e 21ee 2123 21ef 212f cbe7 cb21 cbcb cb6b
  //   cb2d cb6e cbee cb23 cbef cb2f 6be7 6b21 6bcb 6b6b 6b2d 6b6e 6bee 6b23 6bef 6b2f 2de7 2d21 2dcb 2d6b
  //   2d2d 2d6e 2dee 2d23 2def 2d2f 6ee7 6e21 6ecb 6e6b 6e2d 6e6e 6eee 6e23 6eef 6e2f eee7 ee21 eecb ee6b
  //   ee2d ee6e eeee ee23 eeef ee2f 23e7 2321 23cb 236b 232d 236e 23ee 2323 23ef 232f efe7 ef21 efcb ef6b
  //   ef2d ef6e efee ef23 efef ef2f 2fe7 2f21 2fcb 2f6b 2f2d 2f6e 2fee 2f23 2fef 2f2f 21e7e7 21e721 21e7cb
  //   21e76b 21e72d 21e76e 21e7ee 21e723 21e7ef 21e72f 2121e7 212121 2121cb 21216b 21212d 21216e 2121ee
  //   212123 2121ef 21212f 21cbe7 21cb21 21cbcb 21cb6b 21cb2d 21cb6e 21cbee 21cb23 21cbef 21cb2f 216be7
  //   216b21 216bcb 216b6b 216b2d 216b6e 216bee 216b23 216bef 216b2f 212de7 212d21 212dcb 212d6b 212d2d
  //   212d6e 212dee 212d23 212def 212d2f 216ee7 216e21 216ecb 216e6b 216e2d 216e6e 216eee 216e23 216eef
  //   216e2f 21eee7 21ee21 21eecb 21ee6b 21ee2d 21ee6e 21eeee 21ee23 21eeef 21ee2f 2123e7 212321 2123cb
  //   21236b 21232d 21236e 2123ee 212323 2123ef 21232f 21efe7 21ef21 21efcb 21ef6b 21ef2d 21ef6e 21efee
  //   21ef23 21efef 21ef2f 212fe7 212f21 212fcb 212f6b 212f2d 212f6e 212fee 212f23 212fef 212f2f cbe7e7
  //   cbe721 cbe7cb cbe76b cbe72d cbe76e cbe7ee cbe723 cbe7ef cbe72f cb21e7 cb2121 cb21cb cb216b cb212d
  //   cb216e cb21ee cb2123 cb21ef cb212f cbcbe7 cbcb21 cbcbcb cbcb6b cbcb2d cbcb6e cbcbee cbcb23 cbcbef
  //   cbcb2f cb6be7 cb6b21 cb6bcb cb6b6b cb6b2d cb6b6e cb6bee cb6b23 cb6bef cb6b2f cb2de7 cb2d21 cb2dcb
  //   cb2d6b cb2d2d cb2d6e cb2dee cb2d23 cb2def cb2d2f cb6ee7 cb6e21 cb6ecb cb6e6b cb6e2d cb6e6e
endmodule

module CU (
  input  OPC7,
  input  OPC6,
  input  OPC5,
  input  OPC4,
  input  OPC3,
  input  OPC2,
  input  OPC1,
  input  OPC0,
  input  SC2,
  input  SC1,
  input  SC0,
  output C0,
  output C1,
  output C2,
  output C3,
  output C4,
  output C5,
  output C6,
  output C7,
  output C8,
  output C9,
  output C10,
  output C11,
  output C12,
  output C13,
  output C14,
  output C15
);

  wire and_4_out, and_5_out, and_6_out, and_7_out, and_8_out, and_9_out, and_10_out, and_13_out, and_14_out,
       and_15_out, and_16_out, and_17_out, and_18_out, and_19_out, and_20_out, not_1_out, not_2_out,
       not_3_out, not_4_out, not_5_out;

  not not_1 (not_1_out, OPC1);
  not not_2 (not_2_out, OPC0);
  not not_3 (not_3_out, SC2);
  not not_4 (not_4_out, SC1);
  not not_5 (not_5_out, SC0);
  and and_1 (C0, not_3_out, not_4_out, not_5_out);
  and and_2 (C1, not_3_out, not_4_out, SC0);
  and and_3 (C2, OPC1, OPC0, SC2, not_4_out, not_5_out);
  and and_4 (and_4_out, not_3_out, not_4_out, SC0);
  and and_5 (and_5_out, not_1_out, SC2, not_4_out, not_5_out);
  and and_6 (and_6_out, not_3_out, not_4_out, SC0);
  and and_7 (and_7_out, not_1_out, SC2, not_4_out, not_5_out);
  and and_8 (and_8_out, OPC1, OPC0, not_3_out, SC0);
  and and_9 (and_9_out, not_3_out, SC1, not_5_out);
  and and_10 (and_10_out, not_1_out, SC2, not_4_out, SC0);
  and and_11 (C6, OPC1, OPC0, SC2, not_4_out, not_5_out);
  and and_12 (C7, not_3_out, SC1, not_5_out);
  and and_13 (and_13_out, not_1_out, not_3_out, SC1, SC0);
  and and_14 (and_14_out, OPC0, not_3_out, SC1, SC0);
  and and_15 (and_15_out, not_3_out, not_4_out, not_5_out);
  and and_16 (and_16_out, not_1_out, not_3_out, SC1, SC0);
  and and_17 (and_17_out, OPC0, not_3_out, SC1, SC0);
  and and_18 (and_18_out, not_3_out, not_4_out, SC0);
  and and_19 (and_19_out, not_1_out, SC2, not_4_out, not_5_out);
  and and_20 (and_20_out, OPC0, SC2, not_4_out, not_5_out);
  and and_21 (C11, OPC1, not_2_out, not_3_out, SC1, SC0);
  and and_22 (C12, not_1_out, not_2_out, SC2, not_4_out, SC0);
  and and_23 (C13, not_1_out, OPC0, SC2, not_4_out, SC0);
  and and_24 (C14, OPC1, OPC0, not_3_out, SC1, SC0);
  and and_25 (C15, OPC1, not_2_out, not_3_out, SC1, SC0);
  or or_1 (C3, and_4_out, and_5_out);
  or or_2 (C4, and_6_out, and_7_out, and_8_out);
  or or_3 (C5, and_9_out, and_10_out);
  or or_4 (C8, and_13_out, and_14_out);
  or or_5 (C9, and_15_out, and_16_out, and_17_out);
  or or_6 (C10, and_18_out, and_19_out, and_20_out);
endmodule
